// Logisim project control_logic.circ as structural Verilog: 6 circuits, main circuit control_logic
module control_logic (
  input  [31:0] inst,
  input  BrEq,
  input  BrLt,
  output PCSel,
  output RegWEn,
  output [2:0] ImmSel,
  output BrUn,
  output ASel,
  output BSel,
  output [3:0] ALUSel,
  output MemRW,
  output [1:0] WBSel,
  output BrSel
);

  RegWEn_processor regwen_processor_1 (.Opcode(inst[6:0]), .RegWEn(RegWEn));
  ASel_processor asel_processor_1 (.Opcode(inst[6:0]), .ASel(ASel));
  MemRW_processor memrw_processor_1 (.Opcode(inst[6:0]), .func3(inst[14:12]), .BrEq(BrEq), .BrLt(BrLt), .MemRW(MemRW));
  BrUn_processor brun_processor_1 (.Opcode(inst[6:0]), .func3(inst[14:12]), .BrUn(BrUn));
  BSel_processor bsel_processor_1 (.Opcode(inst[6:0]), .BSel(BSel));

  // Other names for the same wires on the sheet: Opcode[6:0] = inst[6:0]; func3[2:0] = inst[14:12];
  //   func7[6:0] = inst[31:25]

  // Notes on the sheet:
  //   INPUTS to your circuit
  //   DON'T CHANGE THE LOCATIONS OF THE INPUTS AND OUTPUTS!
  //   OUTPUT from your circuit
endmodule

module RegWEn_processor (
  input  [6:0] Opcode,
  output RegWEn
);

  wire and_1_out, not_1_out, not_2_out, not_3_out;

  not not_1 (not_1_out, Opcode[2]);
  not not_2 (not_2_out, Opcode[3]);
  not not_3 (not_3_out, Opcode[4]);
  and and_1 (and_1_out, not_1_out, not_2_out, not_3_out, Opcode[5]);
  not not_4 (RegWEn, and_1_out);

  // Notes on the sheet:
  //   INPUT
  //   OUTPUT
endmodule

module BrUn_processor (
  input  [6:0] Opcode,
  input  [2:0] func3,
  output BrUn
);

  wire not_1_out, not_2_out, not_3_out;

  not not_1 (not_1_out, Opcode[2]);
  not not_2 (not_2_out, Opcode[3]);
  not not_3 (not_3_out, Opcode[4]);
  and and_1 (BrUn, not_1_out, not_2_out, not_3_out, Opcode[5], Opcode[6], func3[1], func3[2]);

  // Notes on the sheet:
  //   INPUT
  //   OUTPUT
endmodule

module ASel_processor (
  input  [6:0] Opcode,
  output ASel
);

  wire ASel_B, ASel_J, ASel_U, not_1_out, not_2_out, not_3_out, not_4_out, not_5_out, not_6_out;

  not not_1 (not_1_out, Opcode[2]);
  not not_2 (not_2_out, Opcode[3]);
  not not_3 (not_3_out, Opcode[4]);
  not not_4 (not_4_out, Opcode[4]);
  not not_5 (not_5_out, Opcode[3]);
  not not_6 (not_6_out, Opcode[6]);
  and and_1 (ASel_B, not_1_out, not_2_out, not_3_out, Opcode[5], Opcode[6]);
  and and_2 (ASel_J, Opcode[2], Opcode[3], not_4_out, Opcode[5], Opcode[6]);
  and and_3 (ASel_U, Opcode[2], not_5_out, Opcode[4], not_6_out);
  or or_1 (ASel, ASel_B, ASel_J, ASel_U);

  // Notes on the sheet:
  //   INPUT
  //   OUTPUT
endmodule

module BSel_processor (
  input  [6:0] Opcode,
  output BSel
);

  wire and_1_out, not_1_out, not_2_out, not_3_out;

  not not_1 (not_1_out, Opcode[2]);
  not not_2 (not_2_out, Opcode[3]);
  not not_3 (not_3_out, Opcode[6]);
  and and_1 (and_1_out, not_1_out, not_2_out, Opcode[4], Opcode[5], not_3_out);
  not not_4 (BSel, and_1_out);

  // Notes on the sheet:
  //   INPUT
  //   OUTPUT
endmodule

module MemRW_processor (
  input  [6:0] Opcode,
  input  [2:0] func3,
  input  BrEq,
  input  BrLt,
  output MemRW
);

  wire and_1_out, is_S, is_sw, not_1_out, not_2_out, not_3_out, not_4_out, not_5_out, not_6_out;

  not not_1 (not_1_out, Opcode[2]);
  not not_2 (not_2_out, Opcode[3]);
  not not_3 (not_3_out, Opcode[4]);
  not not_4 (not_4_out, Opcode[6]);
  not not_5 (not_5_out, func3[0]);
  not not_6 (not_6_out, func3[2]);
  and and_1 (and_1_out, not_1_out, not_2_out, not_3_out, Opcode[5], not_4_out);
  and and_2 (is_sw, not_5_out, func3[1], not_6_out);
  not not_7 (is_S, and_1_out);
  and and_3 (MemRW, is_S, is_sw);

  // Notes on the sheet:
  //   INPUT
  //   OUTPUT
endmodule
