// Logisim project cpu.circ as structural Verilog: 1 circuit, main circuit main
module main (
  input  [31:0] INSTRUCTION,
  input  CLOCK,
  output [31:0] PROGRAM_COUNTER,
  output [31:0] ra,
  output [31:0] sp,
  output [31:0] t0,
  output [31:0] t1,
  output [31:0] t2,
  output [31:0] s0,
  output [31:0] s1,
  output [31:0] a0
);

  wire AddrSel, ASel, BrEq, BrLt, BrSel, BrUn, BSel, MemRW, PCSel, RegWEn;
  wire [1:0] WBSel;
  wire [2:0] ImmSel;
  wire [3:0] ALUSel;
  wire [31:0] adder_1_out, alu_out, imm, INSTRUCTION_OUT, multiplexer_1_out, rs1_out, rs2_out;

  control_logic control_logic_1 (
    .BSel(BSel), .ImmSel(ImmSel), .BrLt(BrLt), .BrUn(BrUn), .RegWEn(RegWEn), .ASel(ASel), .PCSel(PCSel),
    .BrEq(BrEq), .inst(INSTRUCTION_OUT), .ALUSel(ALUSel), .MemRW(MemRW), .WBSel(WBSel), .AddrSel(AddrSel),
    .BrSel(BrSel));
  Multiplexer #(.width(32), .enable("false")) multiplexer_1 (
    .in0(rs2_out), .in1(imm), .out(multiplexer_1_out), .sel(BrSel));
  imm_gen imm_gen_1 (.ImmSel(ImmSel), .inst(INSTRUCTION_OUT), .imm(imm));
  branch_comp branch_comp_1 (.BrEq(BrEq), .BrUn(BrUn), .rs1(rs1_out), .BrLt(BrLt), .rs2(multiplexer_1_out));
  Adder #(.width(32)) adder_1 (.a(PROGRAM_COUNTER), .b(32'h4), .out(adder_1_out));  // open: cin, cout
  Register #(.width(32)) PC (.D(adder_1_out), .clk(CLOCK), .Q(PROGRAM_COUNTER));  // open: en, clr
  Register #(.width(32)) register_1 (.D(INSTRUCTION), .clk(CLOCK), .Q(INSTRUCTION_OUT));  // open: en, clr
  alu Arithmetic_Logic_Unit (.Result(alu_out), .ALUSel(4'b0000), .A(rs1_out), .B(imm));
  regfile_main RegFile (
    .rs2(INSTRUCTION_OUT[24:20]), .rd(INSTRUCTION_OUT[11:7]), .Read_Data_1(rs1_out), .Read_Data_2(rs2_out),
    .ra(ra), .sp(sp), .t0(t0), .t1(t1), .t2(t2), .s0(s0), .s1(s1), .a0(a0), .rs1(INSTRUCTION_OUT[19:15]),
    .Write_Data(alu_out), .RegWEn(RegWEn), .clk(CLOCK));
  // mem_main DMEM: pin names not known

  // Other names for the same wires on the sheet: clk = CLOCK; rd_in[4:0] = INSTRUCTION_OUT[11:7];
  //   rs1_in[4:0] = INSTRUCTION_OUT[19:15]; rs2_in[4:0] = INSTRUCTION_OUT[24:20]

  // Notes on the sheet:
  //   Output
  //   IMEM (do **NOT** move this)
  //   Inputs
  //   It is OK to move the PC, RegFile, ALU, MEM, Branch Comp, Imm Gen, and Control Logic to wherever is most convenient for you when constructing your CPU, and to delete this text
  //   Inputs/Outputs for testing. Do **NOT** move these.
endmodule
